// Logisim project Security_Sys.circ as structural Verilog: 3 circuits, main circuit main
module main (
  input  in_1,
  input  in_2,
  input  in_3,
  input  in_4,
  input  in_5,
  input  ENTER_BUTTON,
  input  INPUT_PASSWORD,
  input  in_8,
  input  in_9,
  input  in_10,
  input  in_11,
  input  in_12,
  output Q0,
  output Q1
);

  wire and_1_out, and_2_out, and_3_out, and_4_out, button_1_out, not_1_out, xnor_1_out, xnor_2_out,
       xnor_3_out, xnor_4_out, xnor_5_out;

  xnor xnor_1 (xnor_1_out, in_1, INPUT_PASSWORD);
  xnor xnor_2 (xnor_2_out, in_2, in_8);
  xnor xnor_3 (xnor_3_out, in_3, in_9);
  xnor xnor_4 (xnor_4_out, in_4, in_10);
  xnor xnor_5 (xnor_5_out, in_5, in_11);
  Button button_1 (.out(button_1_out));
  and and_1 (and_1_out, xnor_1_out, xnor_2_out, xnor_3_out, xnor_4_out, xnor_5_out);
  J_K_Flip_Flop j_k_ff_1 (
    .J(and_3_out), .clk(button_1_out), .K(and_3_out), .Q(Q0), .reset(and_2_out));  // open: Qn, preset, en
  not not_1 (not_1_out, and_1_out);
  J_K_Flip_Flop j_k_ff_2 (.J(Q0), .clk(button_1_out), .K(Q0), .Q(Q1), .reset(and_2_out));  // open: Qn, preset, en
  and and_2 (and_2_out, and_1_out, ENTER_BUTTON);
  and and_3 (and_3_out, not_1_out, ENTER_BUTTON);
  LED led_1 (.in(and_3_out));
  LED led_2 (.in(and_2_out));
  and and_4 (and_4_out, Q1, Q0);
  Hex_Digit_Display hex_digit_display_1 (.value({{2{in_12}}, Q1, Q0}));  // open: dp
  LED led_3 (.in(and_4_out));

  // Notes on the sheet:
  //   SET PASSWORD
  //   GO
  //   STOP
  //   ALARM
endmodule

module demo2 (
  input  in_1,
  input  in_2,
  input  in_3,
  input  in_4,
  input  in_5,
  input  in_6,
  input  in_7,
  input  in_8,
  input  in_9,
  input  in_10,
  input  in_11,
  input  in_12,
  output Q1,
  output Q0
);

  wire clock_1_out, nor_1_out, nor_2_out, nor_3_out, nor_4_out, nor_5_out, nor_6_out, nor_7_out, nor_8_out,
       not_1_out, not_2_out, not_7_out;

  nor nor_1 (nor_1_out, in_2, in_7);
  nor nor_2 (nor_2_out, in_3, in_8);
  nor nor_3 (nor_3_out, in_4, in_9);
  nor nor_4 (nor_4_out, in_5, in_10);
  nor nor_5 (nor_5_out, in_6, in_11);
  Clock clock_1 (.out(clock_1_out));
  not not_1 (not_1_out, clock_1_out);
  not not_2 (not_2_out, nor_1_out);
  not not_3 (not_2_out, nor_2_out);
  not not_4 (not_2_out, nor_3_out);
  not not_5 (not_2_out, nor_4_out);
  not not_6 (not_2_out, nor_5_out);
  J_K_Flip_Flop j_k_ff_1 (.J(1'b1), .clk(not_1_out), .K(1'b1), .Q(Q0));  // open: Qn, preset, en, reset
  not not_7 (not_7_out, Q0);
  nor nor_6 (nor_6_out, not_2_out, not_2_out);
  J_K_Flip_Flop j_k_ff_2 (.J(not_7_out), .clk(not_1_out), .K(not_7_out), .Q(Q1));  // open: Qn, preset, en, reset
  nor nor_7 (nor_7_out, not_2_out, in_1);
  nor nor_8 (nor_8_out, in_1, nor_6_out);
  LED led_1 (.in(nor_8_out));
  LED led_2 (.in(nor_7_out));
  Hex_Digit_Display hex_digit_display_1 (.value({{2{in_12}}, Q1, Q0}));  // open: dp
endmodule

module demo3 (
);

  wire clock_1_out, j_k_ff_1_q, not_1_out;

  Clock clock_1 (.out(clock_1_out));
  not not_1 (not_1_out, clock_1_out);
  J_K_Flip_Flop j_k_ff_1 (.clk(not_1_out), .Q(j_k_ff_1_q));  // open: J, K, Qn, preset, en, reset
  // NOT_Gate not_2 has open pins: in=j_k_ff_1_q, out=open
endmodule
